# Fritzing sketch EsquemaEletricoTCC (saved by Fritzing 0.9.9b)
breadboards: 1

parts:
  MH-ET_LIVE_ESP32_DEVKIT1 = MH-ET LIVE ESP32 DEVKIT 38 pins
  PIR1 = PIR sensor
  DHT1 = DHT11 Humitidy and Temperature Sensor
  M1 = DC Motor
  U1 = LCD-16X2 [package=lcd-16x2_nosilk]
  LCM1602_IIC1 = LCM1602 IIC [part_number="LCM1602 IIC" chip_label="LCM1602 IIC" package="DIP (Dual Inline) [THT]"]
  M2 = Dagu DGServo 9g (Top view) [part_number=RS001B]
  LED1 = LEDs [package=led10mm]
  LED3 = LEDs [package=led10mm]
  LED4 = LEDs [package=led10mm]
  Componente1 = FC-28 Soil Hygrometer Module - Probe
  Componente2 = FC-28 Soil Hygrometer Module
  U2 = 4-Channel 5v Relay Shield [package=relay-4ch5v10a]
  LED2 = LEDs [package=led10mm]
  Componente3 = Breadboard Power Supply Board SMD

nets:
  3V3: MH-ET_LIVE_ESP32_DEVKIT1.3V3, PIR1.VDD, Componente2.VCC
  N1: MH-ET_LIVE_ESP32_DEVKIT1.IO35, Componente2.AO
  N2: MH-ET_LIVE_ESP32_DEVKIT1.IO25, LED2.A
  GND: MH-ET_LIVE_ESP32_DEVKIT1.GND#58, DHT1.GND, LCM1602_IIC1.GND, M2.gnd, LED2.C
  N3: MH-ET_LIVE_ESP32_DEVKIT1.IO13, M2.pulse
  5V: MH-ET_LIVE_ESP32_DEVKIT1.5V, DHT1.VDD, LCM1602_IIC1.VCC
  GND_2: MH-ET_LIVE_ESP32_DEVKIT1.GND#64, PIR1.GND, Componente2.GND
  N4: MH-ET_LIVE_ESP32_DEVKIT1.IO23, U2.IN1
  N5: MH-ET_LIVE_ESP32_DEVKIT1.IO22, LCM1602_IIC1.SCL
  N6: MH-ET_LIVE_ESP32_DEVKIT1.IO21, LCM1602_IIC1.SDA
  N7: MH-ET_LIVE_ESP32_DEVKIT1.IO19, U2.IN4
  N8: MH-ET_LIVE_ESP32_DEVKIT1.IO18, U2.IN2
  N9: MH-ET_LIVE_ESP32_DEVKIT1.IO5, U2.IN3
  N10: MH-ET_LIVE_ESP32_DEVKIT1.IO2, PIR1.SIG
  N11: MH-ET_LIVE_ESP32_DEVKIT1.IO15, DHT1.DATA
  N12: M1.pin_1, U2.K4-On
  VCC: M1.pin_2, LED1.C, U2.VCC, Componente3.VCC
  VSS: U1.VSS, LCM1602_IIC1.VSS
  VDD: U1.VDD, LCM1602_IIC1.VDD
  N13: U1.VO, LCM1602_IIC1.V0
  N14: U1.RS, LCM1602_IIC1.RS
  N15: U1.R_W, LCM1602_IIC1.RW
  N16: U1.E, LCM1602_IIC1.E
  N17: U1.DB0, LCM1602_IIC1.D0
  N18: U1.DB1, LCM1602_IIC1.D1
  N19: U1.DB2, LCM1602_IIC1.D2
  N20: U1.DB3, LCM1602_IIC1.D3
  N21: U1.DB4, LCM1602_IIC1.D4
  N22: U1.DB5, LCM1602_IIC1.D5
  N23: U1.DB6, LCM1602_IIC1.D6
  N24: U1.DB7, LCM1602_IIC1.D7
  N25: U1.A, LCM1602_IIC1.A
  N26: U1.K, LCM1602_IIC1.K
  N27: LED1.A, U2.K1-Off
  N28: LED3.A, U2.K2-Off
  N29: LED4.A, U2.K3-Off
  N30: Componente1.POS, Componente2.POS
  N31: Componente1.NEG, Componente2.NEG
  GND_3: U2.GND, U2.K1-On, U2.K2-On, U2.K3-On, U2.K4-Off, Componente3.GND

custom parts:
  MH-ET LIVE ESP32 DEVKIT 38 pins: http://mh.nodebb.com/topic/2/mh-et-live-esp32-devkit
  DHT11 Humitidy and Temperature Sensor: DHT11 Humidity and Temperature Sensor
  LCM1602 IIC: I2C-Module to use a 1602 or 2004 LCD on with the wire.h libory Serial LCD Modul
  FC-28 Soil Hygrometer Module - Probe: The FC-28 is a soil hygrometer module that uses the Texas Instruments LM393 comparator chip to provide an analog measurement of soil humidity.
  FC-28 Soil Hygrometer Module: The FC-28 is a soil hygrometer module that uses the Texas Instruments LM393 comparator chip to provide an analog measurement of soil humidity. The digital output is high when soil moisture is over a certain threshold, as determined by adjusting the potentiometer.
  4-Channel 5v Relay Shield: 4 Channel 5v Relay Shield w. 2x SPD-06VDC-SD-C
